# Fritzing sketch thermo (saved by Fritzing 0.9.3b)
circuit board: 8.46667cm x 5.64444cm

parts:
  IC1 = IC, DIP package, 14 pins [chip_label=IC]
  IC2 = IC, DIP package, 14 pins [chip_label=IC]
  J1 = Screw terminal - 2 pins [package=THT]
  J2 = Screw terminal - 2 pins [package=THT]
  C1 = Ceramic Capacitor [capacitance=1µF package="100 mil [THT, multilayer]"]
  J3 = female pin header, 4 pins [form="♀ (female)"]
  C2 = Ceramic Capacitor [capacitance=1µF package="100 mil [THT, multilayer]"]

nets:
  N1: IC1.pin1, IC1.pin4, IC1.pin7, IC1.pin13, IC2.pin1, IC2.pin4, IC2.pin7, IC2.pin13, J1.pin1, J2.pin1, C1.0, J3.pin2, C2.0
  N2: IC1.pin8, IC1.pin9, J3.pin3
  N3: IC1.pin11, IC2.pin11, J3.pin1
  N4: IC1.pin14, J2.pin2, C2.1
  N5: IC2.pin8, IC2.pin9, J3.pin4
  N6: IC2.pin14, J1.pin2, C1.1
